// Logisim project SPM.circ as structural Verilog: 2 circuits, main circuit main
module main (
  input  y__serial_in,
  input  x0,
  input  x1,
  input  x2,
  input  x3,
  input  x4,
  input  x5,
  input  x6,
  input  x7,
  input  in_10,
  output serial_output
);

  wire and_1_out, and_2_out, and_3_out, and_4_out, and_5_out, and_6_out, and_7_out, clock_1_out, csadd_2_sum,
       csadd_3_sum, csadd_4_sum, csadd_5_sum, csadd_6_sum, csadd_7_sum, undriven;

  Clock clock_1 (.out(clock_1_out));
  and and_1 (and_1_out, x0, y__serial_in);
  and and_2 (and_2_out, x1, y__serial_in);
  and and_3 (and_3_out, x2, y__serial_in);
  and and_4 (and_4_out, x3, y__serial_in);
  and and_5 (and_5_out, x4, y__serial_in);
  and and_6 (and_6_out, x5, x5, y__serial_in);
  and and_7 (and_7_out, x6, y__serial_in);
  // AND_Gate and_8 has open pins: in1=x7, in2=y__serial_in, out=open
  CSADD csadd_1 (.X(and_1_out), .Y(csadd_2_sum), .HSUM1(clock_1_out), .rst(in_10), .SUM(serial_output));
  CSADD csadd_2 (.X(and_2_out), .Y(csadd_3_sum), .HSUM1(clock_1_out), .rst(in_10), .SUM(csadd_2_sum));
  CSADD csadd_3 (.X(and_3_out), .Y(csadd_4_sum), .HSUM1(clock_1_out), .rst(in_10), .SUM(csadd_3_sum));
  CSADD csadd_4 (.X(and_4_out), .Y(csadd_5_sum), .HSUM1(clock_1_out), .rst(in_10), .SUM(csadd_4_sum));
  CSADD csadd_5 (.X(and_5_out), .Y(csadd_6_sum), .HSUM1(clock_1_out), .rst(in_10), .SUM(csadd_5_sum));
  CSADD csadd_6 (.X(and_6_out), .Y(csadd_7_sum), .HSUM1(clock_1_out), .rst(in_10), .SUM(csadd_6_sum));
  CSADD csadd_7 (.X(and_7_out), .Y(undriven), .HSUM1(clock_1_out), .rst(in_10), .SUM(csadd_7_sum));

  // Notes on the sheet:
  //   reset
  //   clk
  //   from TCMP
endmodule

module CSADD (
  input  X,
  input  Y,
  input  HSUM1,
  input  rst,
  output SUM
);

  wire adder_1_cout, adder_1_out, and_1_out, and_2_out, clock_1_out, d_ff_2_q, not_1_out, xor_1_out,
       xor_2_out;

  Clock clock_1 (.out(clock_1_out));
  Adder #(.width(1)) adder_1 (.a(Y), .b(d_ff_2_q), .out(adder_1_out), .cin(HSUM1), .cout(adder_1_cout));
  not not_1 (not_1_out, rst);
  and and_1 (and_1_out, X, adder_1_out);
  xor xor_1 (xor_1_out, X, adder_1_out);
  D_Flip_Flop #(.trigger("high")) d_ff_1 (
    .clk(clock_1_out), .D(xor_1_out), .Q(SUM), .reset(not_1_out));  // open: Qn, preset, en
  and and_2 (and_2_out, and_1_out, adder_1_cout);
  xor xor_2 (xor_2_out, and_1_out, adder_1_cout);
  D_Flip_Flop #(.trigger("high")) d_ff_2 (
    .clk(clock_1_out), .D(xor_2_out), .Q(d_ff_2_q), .reset(not_1_out));  // open: Qn, preset, en

  // Notes on the sheet:
  //   clk
  //   FDHA
  //   CAR1
  //   FDHA
  //   SC
endmodule
